// Logisim project 3x3 adder_carry ripple.circ as structural Verilog: 3 circuits, main circuit HALF ADDER
module HALF_ADDER (
  input  X,
  input  Y,
  output R,
  output C
);

  and and_1 (C, X, Y);
  xor xor_1 (R, X, Y);
endmodule

module FULL_ADDER (
  input  X,
  input  Y,
  input  Cin,
  output S,
  output Cout
);

  wire half_adder_1_c, half_adder_1_r, half_adder_2_c;

  HALF_ADDER half_adder_1 (.X(X), .R(half_adder_1_r), .C(half_adder_1_c), .Y(Y));
  HALF_ADDER half_adder_2 (.X(half_adder_1_r), .R(S), .C(half_adder_2_c), .Y(Cin));
  or or_1 (Cout, half_adder_2_c, half_adder_1_c);
endmodule

module _3x3_adder (
  input  [2:0] in_1,
  input  [2:0] in_2,
  input  in_3,
  output out_4,
  output [2:0] out_5
);

  wire full_adder_1_cout, full_adder_3_cout;

  FULL_ADDER full_adder_1 (.X(in_1[1]), .Y(in_2[1]), .Cin(full_adder_3_cout), .S(out_5[1]), .Cout(full_adder_1_cout));
  FULL_ADDER full_adder_2 (.X(in_1[2]), .Y(in_2[2]), .Cin(full_adder_1_cout), .S(out_5[2]), .Cout(out_4));
  FULL_ADDER full_adder_3 (.X(in_1[0]), .Y(in_2[0]), .Cin(in_3), .S(out_5[0]), .Cout(full_adder_3_cout));
endmodule
