// Logisim project 3x3 subtractor_borrow ripple.circ as structural Verilog: 3 circuits, main circuit HALF ADDER
module HALF_ADDER (
  input  X,
  input  Y,
  output R,
  output B
);

  wire not_1_out;

  not not_1 (not_1_out, X);
  xor xor_1 (R, X, Y);
  and and_1 (B, not_1_out, Y);
endmodule

module FULL_ADDER (
  input  X,
  input  Y,
  input  Bin,
  output D,
  output Bout
);

  wire half_adder_1_b, half_adder_1_r, half_adder_2_b;

  HALF_ADDER half_adder_1 (.X(X), .R(half_adder_1_r), .Y(Y), .B(half_adder_1_b));
  HALF_ADDER half_adder_2 (.X(half_adder_1_r), .R(D), .Y(Bin), .B(half_adder_2_b));
  or or_1 (Bout, half_adder_2_b, half_adder_1_b);
endmodule

module _3x3_subtractor (
  input  [2:0] X,
  input  [2:0] Y,
  input  Bin,
  output Bout,
  output [2:0] D
);

  wire full_adder_2_bout, full_adder_3_bout;

  FULL_ADDER full_adder_1 (.X(X[2]), .Y(Y[2]), .Bin(full_adder_2_bout), .D(D[2]), .Bout(Bout));
  FULL_ADDER full_adder_2 (.X(X[1]), .Y(Y[1]), .Bin(full_adder_3_bout), .D(D[1]), .Bout(full_adder_2_bout));
  FULL_ADDER full_adder_3 (.X(X[0]), .Y(Y[0]), .Bin(Bin), .D(D[0]), .Bout(full_adder_3_bout));
endmodule
