// Logisim project example.circ as structural Verilog: 1 circuit, main circuit main
module main (
  input  in_1,
  input  in_2,
  input  in_3,
  output out_4,
  output out_5
);

  wire transistor_3_out;

  Transistor transistor_1 (.in(1'b1), .out(out_4), .gate(in_1));
  Transistor #(.\type ("n")) transistor_2 (.in(transistor_3_out), .out(out_4), .gate(in_1));
  Transistor #(.\type ("n")) transistor_3 (.in(1'b0), .out(transistor_3_out), .gate(in_2));
  Transistor #(.gate("br")) transistor_4 (.in(1'b1), .out(out_4), .gate(in_2));
endmodule
